# Fritzing sketch SchematBudzika (saved by Fritzing 1.0.4)
breadboards: 2

parts:
  Part1 = Arduino Uno (Rev3) - ICSP
  U1 = LCD-16X2 [package=lcd-16x2]
  LCM1602_IIC1 = LCM1602 IIC [part_number="LCM1602 IIC" chip_label="LCM1602 IIC" package="DIP (Dual Inline) [THT]"]
  U2 = 74HC595 [package="DIP16 [THT]"]
  R2 = Resistor [tolerance=±5% resistance=220 package="2512 [SMD]"]
  R3 = Resistor [tolerance=±5% resistance=220 package="2512 [SMD]"]
  R9 = Resistor [tolerance=±5% resistance=220 package="2512 [SMD]"]
  R10 = Resistor [tolerance=±5% resistance=220 package="2512 [SMD]"]
  R11 = Resistor [tolerance=±5% resistance=220 package="2512 [SMD]"]
  R12 = Resistor [tolerance=±5% resistance=220 package="2512 [SMD]"]
  R13 = Resistor [tolerance=±5% resistance=220 package="2512 [SMD]"]
  R14 = Resistor [tolerance=±5% resistance=220 package="2512 [SMD]"]
  7_Segment_4_Digit_Display1 = 7-SEGMENT-4DIGIT common cathode [part_number=HS420561K-32 package=7-segment-4digit-cathode]
  YwRobot_Power_Supply1 = YwRobot Breadboard Power Supply [part_number=545043]
  U3 = ESP8266 WiFi Module [part_number=ESP8266]
  R15 = Resistor [tolerance=±5% resistance=220 package=THT]
  R16 = Resistor [tolerance=±5% resistance=220 power=0.25W package=THT]

nets:
  N1: Part1.A4/SDA, LCM1602_IIC1.SDA
  N2: Part1.A5/SCL, LCM1602_IIC1.SCL
  N3: Part1.D8, U2.DS
  N4: Part1.D9_PWM, U2.ST_CP
  N5: Part1.D10_PWM/SS, U2.SH_CP
  N6: Part1.D13/SCK, 7_Segment_4_Digit_Display1.pin_6
  GND: Part1.GND, LCM1602_IIC1.GND, U2.GND, U2.OE, YwRobot_Power_Supply1.GND#13, U3.GPIO_0, U3.RST, U3.GND
  N7: Part1.D0/RX, U3.RXD
  N8: Part1.D1/TX, U3.TXD
  VCC: Part1.5V, LCM1602_IIC1.VCC, U2.MR, U2.VCC
  VSS: U1.VSS, LCM1602_IIC1.VSS
  VDD: U1.VDD, LCM1602_IIC1.VDD
  N9: U1.VO, LCM1602_IIC1.V0
  N10: U1.RS, LCM1602_IIC1.RS
  N11: U1.R_W, LCM1602_IIC1.RW
  N12: U1.E, LCM1602_IIC1.E
  N13: U1.DB0, LCM1602_IIC1.D0
  N14: U1.DB1, LCM1602_IIC1.D1
  N15: U1.DB2, LCM1602_IIC1.D2
  N16: U1.DB3, LCM1602_IIC1.D3
  N17: U1.DB4, LCM1602_IIC1.D4
  N18: U1.DB5, LCM1602_IIC1.D5
  N19: U1.DB6, LCM1602_IIC1.D6
  N20: U1.DB7, LCM1602_IIC1.D7
  N21: U1.A, LCM1602_IIC1.A
  N22: U1.K, LCM1602_IIC1.K
  N23: U2.Q1, R13.Pin_0
  N24: U2.Q2, R11.Pin_1
  N25: U2.Q3, R3.Pin_1
  N26: U2.Q4, R2.Pin_1
  N27: U2.Q5, R14.Pin_0
  N28: U2.Q6, R10.Pin_1
  N29: U2.Q7, 7_Segment_4_Digit_Display1.pin_12
  N30: U2.Q0, R9.Pin_0
  N31: R2.Pin_0, 7_Segment_4_Digit_Display1.pin_1
  N32: R3.Pin_0, 7_Segment_4_Digit_Display1.pin_2
  N33: R9.Pin_1, 7_Segment_4_Digit_Display1.pin_11
  N34: R10.Pin_0, 7_Segment_4_Digit_Display1.pin_3
  N35: R11.Pin_0, 7_Segment_4_Digit_Display1.pin_4
  N36: R12.Pin_0, 7_Segment_4_Digit_Display1.pin_5
  N37: R13.Pin_1, 7_Segment_4_Digit_Display1.pin_7
  N38: R14.Pin_1, 7_Segment_4_Digit_Display1.pin_10
  N39: YwRobot_Power_Supply1.VCC#9, U3.VCC, R15.Pin_0, R16.Pin_0
  N40: U3.CH_PD, R15.Pin_1, R16.Pin_1

notes:
  1602A
  3461bs-1

custom parts:
  LCM1602 IIC: I2C-Module to use a 1602 or 2004 LCD on with the wire.h libory Serial LCD Modul
  7-SEGMENT-4DIGIT common cathode: A 7 Segment 4 Digit common cathode display, with decimal points
  YwRobot Breadboard Power Supply: The YwRobot Breadboard Power Supply (MB-V2) has two power rails; they can be 5V or 3V3. Power to the module can be provided through the female USB socket or through the A10 (female) 2.1mm power jack.
  ESP8266 WiFi Module: Generic WiFi Module based on the ESP8266 with onboard PCB antenna and UART communications
